// Logisim project aula2.circ as structural Verilog: 5 circuits, main circuit main
module main (
  input  A0,
  input  A1,
  input  A2,
  input  A3,
  input  F0,
  input  F1,
  input  F2,
  input  B0,
  input  B1,
  input  B2,
  input  B3,
  output S0,
  output S1,
  output S2,
  output S3,
  output Flag_C
);

  wire [3:0] ua4bits_1_s0, ud4bits_1_s0, ul4bits_1_s0;

  UD4bits ud4bits_1 (
    .F0(F0), .A0(A0), .A1(A1), .A2(A2), .A3(A3), .S0(ud4bits_1_s0[0]), .S1(ud4bits_1_s0[1]),
    .S2(ud4bits_1_s0[2]), .S3(ud4bits_1_s0[3]));
  UA4bits ua4bits_1 (
    .A0(A0), .A1(A1), .A2(A2), .A3(A3), .F0(F0), .F1(F1), .B0(B0), .B1(B1), .B2(B2), .B3(B3),
    .S0(ua4bits_1_s0[0]), .S1(ua4bits_1_s0[1]), .S2(ua4bits_1_s0[2]), .S3(ua4bits_1_s0[3]), .Cout(Flag_C));
  UL4bits ul4bits_1 (
    .F0(F0), .A0(A0), .A1(A1), .A2(A2), .A3(A3), .B0(B0), .B1(B1), .B2(B2), .B3(B3), .S0(ul4bits_1_s0[0]),
    .S1(ul4bits_1_s0[1]), .S2(ul4bits_1_s0[2]), .S3(ul4bits_1_s0[3]));
  Multiplexer #(.select(2), .width(4), .enable("false")) multiplexer_1 (
    .in0(ua4bits_1_s0), .in1(ua4bits_1_s0), .in2(ul4bits_1_s0), .in3(ud4bits_1_s0), .out({S3, S2, S1, S0}),
    .sel({F2, F1}));

  // Notes on the sheet:
  //   Entradas
  //   Unidades
  //   Saídas
endmodule

module UA4bits (
  input  A0,
  input  A1,
  input  A2,
  input  A3,
  input  F0,
  input  F1,
  input  B0,
  input  B1,
  input  B2,
  input  B3,
  output S0,
  output S1,
  output S2,
  output S3,
  output Cout
);

  wire adder_1_cout, adder_2_cout, adder_3_cout, uai_1_xi, uai_1_yi, uai_2_xi, uai_2_yi, uai_3_xi, uai_3_yi,
       uai_4_xi, uai_4_yi;

  UAi uai_1 (.Ai(A0), .F1(F1), .F0(F0), .Bi(B0), .Xi(uai_1_xi), .Yi(uai_1_yi));
  UAi uai_2 (.Ai(A1), .F1(F1), .F0(F0), .Bi(B1), .Xi(uai_2_xi), .Yi(uai_2_yi));
  UAi uai_3 (.Ai(A2), .F1(F1), .F0(F0), .Bi(B2), .Xi(uai_3_xi), .Yi(uai_3_yi));
  UAi uai_4 (.Ai(A3), .F1(F1), .F0(F0), .Bi(B3), .Xi(uai_4_xi), .Yi(uai_4_yi));
  Adder #(.width(1)) adder_1 (.a(uai_1_xi), .b(uai_1_yi), .out(S0), .cin(F1), .cout(adder_1_cout));
  Adder #(.width(1)) adder_2 (.a(uai_2_xi), .b(uai_2_yi), .out(S1), .cin(adder_1_cout), .cout(adder_2_cout));
  Adder #(.width(1)) adder_3 (.a(uai_3_xi), .b(uai_3_yi), .out(S2), .cin(adder_2_cout), .cout(adder_3_cout));
  Adder #(.width(1)) adder_4 (.a(uai_4_xi), .b(uai_4_yi), .out(S3), .cin(adder_3_cout), .cout(Cout));
endmodule

// LUA1b
module UAi (
  input  Ai,
  input  F1,
  input  F0,
  input  Bi,
  output Xi,
  output Yi
);

  wire and_2_out, and_3_out, and_4_out, nand_1_out, not_1_out, not_2_out, not_3_out;

  not not_1 (not_1_out, Bi);
  not not_2 (not_2_out, F1);
  not not_3 (not_3_out, F0);
  nand nand_1 (nand_1_out, F1, F0);
  and and_1 (Xi, Ai, nand_1_out);
  and and_2 (and_2_out, not_1_out, F1);
  and and_3 (and_3_out, Bi, not_2_out, F0);
  and and_4 (and_4_out, not_2_out, not_3_out);
  or or_1 (Yi, and_2_out, and_3_out, and_4_out);
endmodule

module UD4bits (
  input  F0,
  input  A0,
  input  A1,
  input  A2,
  input  A3,
  output S0,
  output S1,
  output S2,
  output S3
);

  Multiplexer #(.enable("false")) multiplexer_1 (.in0(A1), .in1(1'b0), .out(S0), .sel(F0));
  Multiplexer #(.enable("false")) multiplexer_2 (.in0(A2), .in1(A0), .out(S1), .sel(F0));
  Multiplexer #(.enable("false")) multiplexer_3 (.in0(A3), .in1(A1), .out(S2), .sel(F0));
  Multiplexer #(.enable("false")) multiplexer_4 (.in0(A3), .in1(A2), .out(S3), .sel(F0));
endmodule

module UL4bits (
  input  F0,
  input  A0,
  input  A1,
  input  A2,
  input  A3,
  input  B0,
  input  B1,
  input  B2,
  input  B3,
  output S0,
  output S1,
  output S2,
  output S3
);

  wire nand_1_out, nand_2_out, nand_3_out, nand_4_out, nor_1_out, nor_2_out, nor_3_out, nor_4_out;

  nand nand_1 (nand_1_out, A0, B0);
  nor nor_1 (nor_1_out, A0, B0);
  nand nand_2 (nand_2_out, A1, B1);
  nor nor_2 (nor_2_out, A1, B1);
  nand nand_3 (nand_3_out, A2, B2);
  nor nor_3 (nor_3_out, A2, B2);
  nand nand_4 (nand_4_out, A3, B3);
  nor nor_4 (nor_4_out, A3, B3);
  Multiplexer #(.disabled(0), .enable("false")) multiplexer_1 (.in0(nand_1_out), .in1(nor_1_out), .out(S0), .sel(F0));
  Multiplexer #(.disabled(0), .enable("false")) multiplexer_2 (.in0(nand_2_out), .in1(nor_2_out), .out(S1), .sel(F0));
  Multiplexer #(.disabled(0), .enable("false")) multiplexer_3 (.in0(nand_3_out), .in1(nor_3_out), .out(S2), .sel(F0));
  Multiplexer #(.disabled(0), .enable("false")) multiplexer_4 (.in0(nand_4_out), .in1(nor_4_out), .out(S3), .sel(F0));
endmodule
