// Logisim project resol.circ as structural Verilog: 1 circuit, main circuit main
module main (
  input  Ai,
  input  Bi,
  input  Ci_1,
  output Ci,
  output out_5
);

  wire and_1_out, and_2_out, and_3_out, and_4_out, and_5_out, and_6_out, and_7_out, not_1_out, not_2_out,
       not_3_out;

  not not_1 (not_1_out, Ai);
  not not_2 (not_2_out, Bi);
  not not_3 (not_3_out, Ci_1);
  and and_1 (and_1_out, Ai, Bi);
  and and_2 (and_2_out, not_1_out, Bi, Ci_1);
  and and_3 (and_3_out, Ai, not_2_out, Ci_1);
  and and_4 (and_4_out, not_1_out, not_2_out, Ci_1);
  and and_5 (and_5_out, not_1_out, Bi, not_3_out);
  and and_6 (and_6_out, Ai, not_2_out, not_3_out);
  and and_7 (and_7_out, Ai, Bi, Ci_1);
  or or_1 (Ci, and_1_out, and_2_out, and_3_out);
  or or_2 (out_5, and_4_out, and_5_out, and_6_out, and_7_out);
endmodule
